// Logisim project CN.circ as structural Verilog: 1 circuit, main circuit main
module main (
  input  [1:0] in_1,
  input  in_2,
  input  [7:0] in_3,
  input  in_4,
  input  [7:0] in_5
);

  wire and_2_out, and_3_out, and_4_out, and_5_out, and_6_out, and_7_out, END_FLAG, multiplexer_7_out, N0,
       nor_1_out, not_2_out, not_3_out, not_6_out, NOT_A8, NOT_S0, NOT_S1, Q_1, SKIP_ALU_SRT2, START, SUB,
       TARGET_REACHED, WE_M, xor_2_out, xor_3_out;
  wire [0:0] SRT2_Q;
  wire [1:0] bit_extender_4_out, CU_SIGNAL, Q, SELECT_M, xor_1_out;
  wire [3:0] counter_1_q, multiplexer_12_out;
  wire [5:0] BOOTH_Q;
  wire [7:0] M, multiplexer_5_out, multiplexer_9_out, Q_SHIFTED;
  wire [8:0] A, A_SHIFTED, ADDER_RESULT, ALU_IN_A, bit_extender_1_out, bit_extender_2_out,
       bit_extender_3_out, BOOTH_A, multiplexer_1_out, multiplexer_3_out, multiplexer_4_out, shifter_1_out,
       xor_4_out;

  Multiplexer #(.select(2), .width(9)) multiplexer_1 (
    .in0(A), .in1({9{1'b0}}), .in2(A), .in3(A_SHIFTED), .out(multiplexer_1_out));  // open: sel
  assign bit_extender_1_out = {{1{M[7]}}, M};  // Bit_Extender bit_extender_1
  xor xor_1 (xor_1_out[0], Q[0], Q_1);
  Register #(.width(9)) u_A (.D(multiplexer_1_out), .en(CU_SIGNAL[0]), .clk(in_2), .Q(A), .clr(in_4));
  Shifter #(.width(9)) shifter_1 (.in(bit_extender_1_out), .\dist (4'b0001), .out(shifter_1_out));
  Multiplexer #(.select(2)) multiplexer_2 (.in0(1'b0), .in1(1'b1), .in2(Q[1]), .in3(NOT_A8), .out(SUB));  // open: sel
  xor xor_2 (xor_2_out, Q[1], Q[0]);
  xor xor_3 (xor_3_out, Q[0], Q_1);
  not not_1 (NOT_A8, A[8]);
  assign bit_extender_2_out = {{8{SUB}}, SUB};  // Bit_Extender bit_extender_2
  Multiplexer #(.select(2), .width(9)) multiplexer_3 (
    .in0({9{1'b0}}), .in1(bit_extender_1_out), .in2(shifter_1_out), .in3({9{1'b0}}), .out(multiplexer_3_out),
    .sel(SELECT_M));
  and and_1 (xor_1_out[1], xor_2_out, not_2_out);
  not not_2 (not_2_out, xor_3_out);
  assign xor_4_out = bit_extender_2_out ^ multiplexer_3_out;  // XOR_Gate xor_4, 9 bits wide
  Multiplexer #(.select(2), .width(9)) multiplexer_4 (
    .in0(bit_extender_3_out), .in1(bit_extender_3_out), .in2(ALU_IN_A), .in3(ALU_IN_A),
    .out(multiplexer_4_out), .sel(in_1));
  assign bit_extender_3_out = {{1{BOOTH_Q[5]}}, {BOOTH_Q, Q}};  // Bit_Extender bit_extender_3
  assign bit_extender_4_out = {{1{1'b0}}, not_3_out};  // Bit_Extender bit_extender_4
  not not_3 (not_3_out, SKIP_ALU_SRT2);
  Register u_Q (.D(multiplexer_5_out), .en(CU_SIGNAL[0]), .clk(in_2), .Q({BOOTH_Q, Q}), .clr(in_4));
  Multiplexer #(.select(2), .width(8)) multiplexer_5 (
    .in0({BOOTH_Q, Q}), .in1(in_3), .in2({BOOTH_Q, Q}), .in3(Q_SHIFTED), .out(multiplexer_5_out));  // open: sel
  Adder #(.width(9)) adder_1 (.a(xor_4_out), .b(multiplexer_4_out), .out(ADDER_RESULT), .cin(SUB));  // open: cout
  Multiplexer #(.select(2), .width(2)) multiplexer_6 (
    .in0(2'b01), .in1(2'b01), .in2(xor_1_out), .in3(bit_extender_4_out), .out(SELECT_M));  // open: sel
  Register #(.width(1)) u_Q_1 (.D(multiplexer_7_out), .en(CU_SIGNAL[0]), .clk(in_2), .Q(Q_1), .clr(in_4));
  Multiplexer #(.select(2)) multiplexer_7 (
    .in0(Q_1), .in1(1'b0), .in2(Q_1), .in3(Q[1]), .out(multiplexer_7_out));  // open: sel
  not not_4 (SRT2_Q[0], ADDER_RESULT[8]);
  Shifter #(.shift("ar"), .width(9)) shifter_2 (.in(ADDER_RESULT), .\dist (4'b0010), .out(BOOTH_A));
  Multiplexer #(.select(2), .width(9)) multiplexer_8 (
    .in0(A), .in1(A), .in2(A), .in3({A[7:0], BOOTH_Q[5]}), .out(ALU_IN_A), .sel(in_1));
  Multiplexer #(.select(2), .width(8)) multiplexer_9 (
    .in0(M), .in1(in_5), .in2(M), .in3(M), .out(multiplexer_9_out));  // open: sel
  not not_5 (NOT_A8, A[7]);
  and and_2 (and_2_out, A[7], A[6], A[5]);
  Register u_M (.D(multiplexer_9_out), .en(WE_M), .clk(in_2), .Q(M), .clr(in_4));
  nor nor_1 (nor_1_out, A[7], A[6], A[5]);
  or or_1 (SKIP_ALU_SRT2, and_2_out, nor_1_out);
  Multiplexer #(.select(2), .width(9)) multiplexer_10 (
    .in0(ADDER_RESULT), .in1(ADDER_RESULT), .in2(BOOTH_A), .in3(ADDER_RESULT), .out(A_SHIFTED));  // open: sel
  Multiplexer #(.select(2), .width(8)) multiplexer_11 (
    .in0({BOOTH_Q, Q}), .in1({BOOTH_Q, Q}), .in2({ADDER_RESULT[1:0], BOOTH_Q}),
    .in3({BOOTH_Q[4:0], Q, SRT2_Q[0]}), .out(Q_SHIFTED), .sel(in_1));
  Button u_START (.out(START));
  Counter #(.max('hf), .width(4)) counter_1 (
    .clr(and_3_out), .up(1'b1), .count(and_4_out), .clk(in_2), .Q(counter_1_q));  // open: load, D, carry
  and and_3 (and_3_out, NOT_S1, CU_SIGNAL[0]);
  and and_4 (and_4_out, CU_SIGNAL[1], CU_SIGNAL[0]);
  Register #(.width(2)) FSM_STATE (.D({CU_SIGNAL[0], N0}), .en(1'b1), .clk(in_2), .Q(CU_SIGNAL), .clr(in_4));
  not not_6 (not_6_out, TARGET_REACHED);
  Multiplexer #(.select(2), .width(4)) multiplexer_12 (
    .in0(4'b0000), .in1(4'b0000), .in2(4'b0011), .in3(4'b0111), .out(multiplexer_12_out), .sel(in_1));
  and and_5 (and_5_out, NOT_S1, NOT_S0, START);
  and and_6 (and_6_out, NOT_S1, CU_SIGNAL[0]);
  and and_7 (and_7_out, CU_SIGNAL[1], CU_SIGNAL[0], not_6_out);
  Comparator #(.mode("unsigned"), .width(4)) comparator_1 (
    .a(counter_1_q), .b(multiplexer_12_out), .eq(TARGET_REACHED));  // open: gt, lt
  not not_7 (NOT_S0, CU_SIGNAL[0]);
  not not_8 (NOT_S1, CU_SIGNAL[1]);
  and and_8 (WE_M, CU_SIGNAL[0], NOT_S1);
  and and_9 (END_FLAG, NOT_S0, CU_SIGNAL[1]);
  or or_2 (N0, and_5_out, and_6_out, and_7_out);

  // Other names for the same wires on the sheet: HOLD_A[8:0] = A; A_IN[7:0] = in_3; BOOTH_Q[7:6] = ADDER_RESULT[1:0];
  //   B_IN[7:0] = in_5; CLK = in_2; N1 = CU_SIGNAL[0]; S0 = CU_SIGNAL[0]; WE_A = CU_SIGNAL[0]; WE_Q = CU_SIGNAL[0];
  //   S1 = CU_SIGNAL[1]; OPCODE[1:0] = in_1; Q[7:2] = BOOTH_Q; RST = in_4; SRT2_Q[7:1] = {BOOTH_Q[4:0], Q}

  // Notes on the sheet:
  //   2*M(M << 1)
  //   SELECT_M[0]
  //   0;M;2M;Don't care
  //   ADD OR SUBSTRACT SELECT_M?
  //   SELECT 0, M OR 2*M?
  //   SRT2 SHIFT Q
  //   BOOTH RADIX4 SHIFT
  //   SRT2 PRE-SHIFT
  //   Select the shift operation result
endmodule
